# Fritzing sketch OpenWeatherDuinoESP8266 (saved by Fritzing 0.9.2b)
circuit board: 8.46667cm x 5.64444cm
breadboards: 1

parts:
  BMP = Barometric Pressure Sensor - BMP085 Breakout
  LM3940/3_3v_Voltage_Regulator = V_REG_LD1117VXX [package=78xxl]
  Arduino_Nano = Arduino Nano (Rev3.0) (ICSP)
  PIN1_VIN_PIN2_DATA_PIN3_GND = female pin header, 3 pins [form="♀ (female)" part_number=DHT11/DHT22]
  LLC = Logic Level Converter
  ESP = double row rounded female pin header, 8 pins [form="♀ (female rounded)"]

nets:
  N1: BMP.VCC, LM3940/3_3v_Voltage_Regulator.OUT, LLC.LV, ESP.pin6, ESP.pin8
  GND: BMP.GND, LM3940/3_3v_Voltage_Regulator.GND, Arduino_Nano.GND, PIN1_VIN_PIN2_DATA_PIN3_GND.pin3, LLC.GND, ESP.pin4
  N2: BMP.SCL, LLC.RX_LV
  N3: BMP.SDA, LLC.RX2_LV
  9V: LM3940/3_3v_Voltage_Regulator.IN, Arduino_Nano.VIN
  N4: Arduino_Nano.D2, PIN1_VIN_PIN2_DATA_PIN3_GND.pin2
  N5: Arduino_Nano.D10, LLC.TX2_HV
  N6: Arduino_Nano.D11/MOSI, LLC.TX_HV
  N7: Arduino_Nano.5V, PIN1_VIN_PIN2_DATA_PIN3_GND.pin1, LLC.HV
  N8: Arduino_Nano.A5, LLC.RX_HV
  N9: Arduino_Nano.A4, LLC.RX2_HV
  N10: LLC.TX2_LV, ESP.pin5
  N11: LLC.TX_LV, ESP.pin1
